# Fritzing sketch Circuit Diagram (saved by Fritzing 1.0.1rc)
breadboards: 1

parts:
  Part1 = Arduino Mega 2560 (Rev3)-TopMount
  J1 = Basic Servo
  J2 = Basic Servo
  J3 = Basic Servo
  J4 = Basic Servo
  HC-SR04_Sensor_1 = HC-SR04 Ultrasonic Distance Sensor
  HC-SR04_Sensor_2 = HC-SR04 Ultrasonic Distance Sensor
  HC-SR04_Sensor_3 = HC-SR04 Ultrasonic Distance Sensor
  HC-SR04_Sensor_4 = HC-SR04 Ultrasonic Distance Sensor
  S1 = H-Bridge with L298N
  M1 = DC Motor [voltage_(max)=6V voltage_(min)=3V]
  M2 = DC Motor [voltage_(max)=6V voltage_(min)=3V]
  Part3 = Bluetooth HC-05 Macho
  BAT1 = BC9VPC [package=bc9vpc]

nets:
  N1: Part1.D19/RX1, Part3.TXD
  N2: Part1.D18/TX1, Part3.RXD
  N3: Part1.D12_PWM, S1.ENA
  N4: Part1.D11_PWM, S1.IN1
  N5: Part1.D10_PWM, S1.IN2
  N6: Part1.D9_PWM, S1.IN3
  N7: Part1.D8_PWM, S1.IN4
  5V: Part1.5V, HC-SR04_Sensor_3.VCC, S1.5V, Part3.VCC
  GND: Part1.GND, HC-SR04_Sensor_3.GND, Part3.GND
  N8: Part1.D2_PWM, J1.pulse
  N9: Part1.D3_PWM, J2.pulse
  N10: Part1.D5_PWM, J4.pulse
  N11: Part1.D6_PWM, J3.pulse
  N12: Part1.D7_PWM, S1.ENB
  N13: Part1.D22, HC-SR04_Sensor_3.ECHO
  N14: Part1.D23, HC-SR04_Sensor_3.TRIG
  N15: Part1.D24, HC-SR04_Sensor_4.ECHO
  N16: Part1.D25, HC-SR04_Sensor_4.TRIG
  N17: Part1.D26, HC-SR04_Sensor_1.ECHO
  N18: Part1.D27, HC-SR04_Sensor_1.TRIG
  N19: Part1.D28, HC-SR04_Sensor_2.ECHO
  N20: Part1.D29, HC-SR04_Sensor_2.TRIG
  N21: S1.12V, BAT1.V+
  N22: S1.GND, BAT1.V-
  N23: S1.M1-01, M1.pin_2
  N24: S1.M1-02, M1.pin_1
  N25: S1.M2-01, M2.pin_1
  N26: S1.M2-02, M2.pin_2

notes:
  MAIN
  LEFT
  RIGHT
  CONTAINER

custom parts:
  Arduino Mega 2560 (Rev3)-TopMount: Arduino Mega 2560 (Rev3) for Top PCB Mount. The PCB view of the Arduino Mega 2560 (Rev3) in Arduino Bin flipped upside down with the text flipped back so as to be readable. Other views haven't changed Protruding component position is outlined to provide indication of part contact. Number in component outline is mm of protrusion of the component from the Mega PCB. Subtract the number from the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
  H-Bridge with L298N: h-bridge
